// Logisim project banc_registre.circ as structural Verilog: 1 circuit, main circuit main
module main (
  input  CLOCK,
  input  RESET,
  input  [31:0] DataIn,
  input  [2:0] Reg_A,
  input  [2:0] RegDest,
  input  [2:0] Reg_B,
  output [31:0] R0,
  output [31:0] A,
  output [31:0] R1,
  output [31:0] R2,
  output [31:0] R3,
  output [31:0] R4,
  output [31:0] B,
  output [31:0] R5,
  output [31:0] R6,
  output [31:0] R7
);

  wire decoder_1_out0, decoder_1_out1, decoder_1_out2, decoder_1_out3, decoder_1_out4, decoder_1_out5,
       decoder_1_out6, decoder_1_out7;

  Decoder #(.select(3), .enable("false")) decoder_1 (
    .out0(decoder_1_out0), .out1(decoder_1_out1), .out2(decoder_1_out2), .out3(decoder_1_out3),
    .out4(decoder_1_out4), .out5(decoder_1_out5), .out6(decoder_1_out6), .out7(decoder_1_out7), .sel(RegDest));
  Register #(.width(32), .trigger("high")) u_R0 (.D(DataIn), .en(decoder_1_out0), .Q(R0), .clk(CLOCK), .clr(CLOCK));
  Register #(.width(32), .trigger("high")) u_R1 (.D(DataIn), .en(decoder_1_out1), .Q(R1), .clk(CLOCK), .clr(CLOCK));
  Register #(.width(32), .trigger("high")) register_1 (
    .D(DataIn), .en(decoder_1_out2), .Q(R2), .clk(CLOCK), .clr(CLOCK));
  Register #(.width(32), .trigger("high")) u_R3 (.D(DataIn), .en(decoder_1_out3), .Q(R3), .clk(CLOCK), .clr(CLOCK));
  Register #(.width(32), .trigger("high")) u_R4 (.D(DataIn), .en(decoder_1_out4), .Q(R4), .clr(CLOCK));  // open: clk
  Register #(.width(32), .trigger("high")) u_R5 (.D(DataIn), .en(decoder_1_out5), .Q(R5), .clk(CLOCK), .clr(CLOCK));
  Register #(.width(32), .trigger("high")) u_R6 (.D(DataIn), .en(decoder_1_out6), .Q(R6), .clk(CLOCK), .clr(CLOCK));
  Register #(.width(32), .trigger("high")) u_R7 (.D(DataIn), .en(decoder_1_out7), .Q(R7), .clk(CLOCK), .clr(CLOCK));
  Multiplexer #(.select(3), .width(32), .enable("false")) multiplexer_1 (
    .in0(R0), .in1(R1), .in2(R2), .in3(R3), .in4(R4), .in5(R5), .in6(R6), .in7(R7), .out(A), .sel(Reg_A));
  Multiplexer #(.select(3), .width(32), .enable("false")) multiplexer_2 (
    .in0(R0), .in1(R1), .in2(R2), .in3(R3), .in4(R4), .in5(R5), .in6(R6), .in7(R7), .out(B), .sel(Reg_B));

  assign RESET = CLOCK;
endmodule
