// Logisim project controler.circ as structural Verilog: 10 circuits, main circuit main
module main (
  input  [15:0] Inst,
  input  [3:0] Flags,
  input  Clk,
  input  Reset,
  output Carry,
  output DP_Shift,
  output Imm32_Enable,
  output [4:0] Imm5,
  output [31:0] Imm32,
  output [3:0] ALU_Opcode,
  output [2:0] Rm,
  output [2:0] Rn,
  output [2:0] Rd,
  output [31:0] RAM_Addr,
  output Load,
  output Store,
  output [7:0] PC
);

  wire Conditionnal_verified, instruction_decoder_a, instruction_decoder_b, instruction_decoder_c,
       instruction_decoder_d, instruction_decoder_e, Load_Store_pc_hold, not_1_out, Shift_Add_Sub_Mov_carry,
       SPAdress_write_enable;
  wire [2:0] dataProcessing_rd, dataProcessing_rm, dataProcessing_rn, Load_Store_rd, Load_Store_rm,
       Shift_Add_Sub_Mov_rd, Shift_Add_Sub_Mov_rm, Shift_Add_Sub_Mov_rn;
  wire [3:0] dataProcessing_alu_opcode, dataProcessing_fum, FlagsAPSR_flagsout, or_1_out,
       Shift_Add_Sub_Mov_codealu, Shift_Add_Sub_Mov_fum;
  wire [7:0] adder_1_out, adder_2_out, Conditionnal_offset;
  wire [31:0] SPAdress_new_stack_pointer, Stack_Pointer_q;

  decoder instruction_decoder (
    .Opcode(Inst[15:10]), .a(instruction_decoder_a), .b(instruction_decoder_b), .c(instruction_decoder_c),
    .d(instruction_decoder_d), .e(instruction_decoder_e));
  Register #(.width(32)) Stack_Pointer (
    .D(SPAdress_new_stack_pointer), .en(SPAdress_write_enable), .Q(Stack_Pointer_q), .clk(Clk), .clr(Reset));
  assign or_1_out = dataProcessing_fum | Shift_Add_Sub_Mov_fum;  // OR_Gate or_1, 4 bits wide
  Shift_add_sub_mov Shift_Add_Sub_Mov (
    .codeAlu(Shift_Add_Sub_Mov_codealu), .Instruction(Inst), .rm(Shift_Add_Sub_Mov_rm),
    .Enable(instruction_decoder_a), .rn(Shift_Add_Sub_Mov_rn), .rd(Shift_Add_Sub_Mov_rd),
    .FUM(Shift_Add_Sub_Mov_fum), .Carry(Shift_Add_Sub_Mov_carry), .Imm32Enable(Imm32_Enable), .Imm5(Imm5),
    .Imm32(Imm32));
  Data_processing dataProcessing (
    .instruction(Inst), .Rm(dataProcessing_rm), .Rn(dataProcessing_rn), .Rd(dataProcessing_rd),
    .ALU_opcode(dataProcessing_alu_opcode), .FUM(dataProcessing_fum), .enable(instruction_decoder_b));
  SP_Address SPAdress (
    .instruction(Inst), .enable(instruction_decoder_d), .Stack_Pointer(Stack_Pointer_q),
    .write_enable(SPAdress_write_enable), .New_Stack_Pointer(SPAdress_new_stack_pointer));
  Conditionnal Conditionnal (
    .Enable(instruction_decoder_e), .Instruction(Inst), .N(FlagsAPSR_flagsout[3]), .Z(FlagsAPSR_flagsout[2]),
    .C(FlagsAPSR_flagsout[1]), .V(FlagsAPSR_flagsout[0]), .Offset(Conditionnal_offset),
    .Verified(Conditionnal_verified));
  FlagAPSR FlagsAPSR (.flagsin(Flags), .FUM(or_1_out), .clk(Clk), .reset(Reset), .flagsout(FlagsAPSR_flagsout));
  Load_Store Load_Store (
    .Store(Store), .instruction(Inst), .Load(Load), .PC_Hold(Load_Store_pc_hold),
    .Stack_pointer(Stack_Pointer_q), .Rm(Load_Store_rm), .Clk(Clk), .Rd(Load_Store_rd), .Reset(Reset),
    .RAM_Address(RAM_Addr), .enable(instruction_decoder_c));
  and and_1 (DP_Shift, instruction_decoder_a, ~instruction_decoder_b);  // AND_Gate
  Adder adder_1 (.a(8'h3), .b(Conditionnal_offset), .out(adder_1_out), .cin(1'b0));  // open: cout
  not not_1 (not_1_out, Load_Store_pc_hold);
  Adder adder_2 (.a(adder_1_out), .b(PC), .out(adder_2_out), .cin(1'b0));  // open: cout
  Multiplexer #(.enable("false")) multiplexer_1 (
    .in0(FlagsAPSR_flagsout[1]), .in1(Shift_Add_Sub_Mov_carry), .out(Carry), .sel(DP_Shift));
  assign ALU_Opcode = Shift_Add_Sub_Mov_codealu | dataProcessing_alu_opcode;  // OR_Gate or_2, 4 bits wide
  assign Rm = Shift_Add_Sub_Mov_rm | dataProcessing_rm | Load_Store_rm;  // OR_Gate or_3, 3 bits wide
  assign Rn = Shift_Add_Sub_Mov_rn | dataProcessing_rn;  // OR_Gate or_4, 3 bits wide
  assign Rd = Shift_Add_Sub_Mov_rd | dataProcessing_rd | Load_Store_rd;  // OR_Gate or_5, 3 bits wide
  Counter counter_1 (
    .load(Conditionnal_verified), .D(adder_2_out), .count(not_1_out), .Q(PC), .clk(Clk), .clr(Reset));  // open: carry

  // Notes on the sheet:
  //   Extract Opcode
  //   Extract carry
endmodule

module Shift_add_sub_mov (
  input  [15:0] Instruction,
  input  Enable,
  output [3:0] codeAlu,
  output [2:0] rm,
  output [2:0] rn,
  output [2:0] rd,
  output [3:0] FUM,
  output Carry,
  output Imm32Enable,
  output [4:0] Imm5,
  output [31:0] Imm32
);

  wire bit9imm, bit9reg, bit10, bit11asr, bit11ls, bit12, bit13, multiplexer_2_out, multiplexer_3_out;
  wire [2:0] bit_extender_4_out, demultiplexer_3_out0_2, demultiplexer_3_out1, instr, multiplexer_7_out,
       multiplexer_8_out, multiplexer_9_out;
  wire [3:0] bit_extender_3_out, multiplexer_1_out, multiplexer_6_out;
  wire [4:0] bit_extender_1_out, multiplexer_4_out;
  wire [15:0] demultiplexer_1_out0, demultiplexer_1_out1, demultiplexer_2_out0, demultiplexer_2_out1,
       demultiplexer_3_out0, demultiplexer_4_out0, demultiplexer_4_out1;
  wire [15:3] demultiplexer_3_out1_2;
  wire [31:0] bit_extender_2_out, multiplexer_5_out;

  BitSelector #(.width(16)) bitselector_1 (.in(Instruction), .out(bit13), .sel(4'b1101));
  Demultiplexer #(.width(16), .enable("false")) demultiplexer_1 (
    .out0(demultiplexer_1_out0), .out1(demultiplexer_1_out1), .in(Instruction), .sel(bit13));
  opcode_decoder opcode_decoder (
    ._1(bit13), ._2(bit12), ._3(bit11ls), ._4(bit11asr), ._5(bit10), ._6(bit9reg), ._7(bit9imm), .instr(instr));
  Demultiplexer #(.width(16), .enable("false")) demultiplexer_2 (
    .out0(demultiplexer_2_out0), .out1(demultiplexer_2_out1), .in(demultiplexer_1_out0), .sel(bit12));
  BitSelector #(.width(16)) bitselector_2 (.in(demultiplexer_1_out0), .out(bit12), .sel(4'b1100));
  Demultiplexer #(.width(16), .enable("false")) demultiplexer_3 (
    .out0({demultiplexer_3_out0[15:6], demultiplexer_3_out0_2, demultiplexer_3_out0[2:0]}),
    .out1({demultiplexer_3_out1_2, demultiplexer_3_out1}), .in(demultiplexer_4_out1), .sel(bit10));
  BitSelector #(.width(16)) bitselector_3 (.in(demultiplexer_4_out1), .out(bit10), .sel(4'b1010));
  BitSelector #(.width(16)) bitselector_4 (.in(demultiplexer_2_out0), .out(bit11ls), .sel(4'b1011));
  Demultiplexer #(.width(16), .enable("false")) demultiplexer_4 (
    .out0(demultiplexer_4_out0), .out1(demultiplexer_4_out1), .in(demultiplexer_2_out1), .sel(bit11asr));
  BitSelector #(.width(16)) bitselector_5 (.in(demultiplexer_2_out1), .out(bit11asr), .sel(4'b1011));
  BitSelector #(.width(16)) bitselector_6 (
    .in({demultiplexer_3_out0[15:6], demultiplexer_3_out0_2, demultiplexer_3_out0[2:0]}), .out(bit9reg),
    .sel(4'b1001));
  BitSelector #(.width(16)) bitselector_7 (
    .in({demultiplexer_3_out1_2, demultiplexer_3_out1}), .out(bit9imm), .sel(4'b1001));
  Multiplexer #(.select(3), .width(4), .enable("false")) multiplexer_1 (
    .in0(4'b1100), .in1(4'b1110), .in2(4'b1110), .in3(4'b1110), .in4(4'b1111), .in5(4'b1111), .in6(4'b1111),
    .in7(4'b1111), .out(multiplexer_1_out), .sel(instr));
  Multiplexer #(.select(3), .enable("false")) multiplexer_2 (
    .in0(1'b0), .in1(1'b0), .in2(1'b0), .in3(1'b0), .in4(1'b0), .in5(1'b1), .in6(1'b0), .in7(1'b1),
    .out(multiplexer_2_out), .sel(instr));
  Multiplexer #(.select(3), .enable("false")) multiplexer_3 (
    .in0(1'b1), .in1(1'b0), .in2(1'b0), .in3(1'b0), .in4(1'b0), .in5(1'b0), .in6(1'b1), .in7(1'b1),
    .out(multiplexer_3_out), .sel(instr));
  Multiplexer #(.select(3), .width(5), .enable("false")) multiplexer_4 (
    .in0({5{1'b0}}), .in1(demultiplexer_2_out0[10:6]), .in2(demultiplexer_2_out0[10:6]),
    .in3(demultiplexer_4_out0[10:6]), .in4({5{1'b0}}), .in5({5{1'b0}}), .in6({5{1'b0}}), .in7({5{1'b0}}),
    .out(multiplexer_4_out), .sel(instr));
  Multiplexer #(.select(3), .width(32), .enable("false")) multiplexer_5 (
    .in0({{24{1'b0}}, demultiplexer_1_out1[7:0]}), .in1({32{1'b0}}), .in2({32{1'b0}}), .in3({32{1'b0}}),
    .in4({32{1'b0}}), .in5({32{1'b0}}), .in6({{29{1'b0}}, demultiplexer_3_out1_2[8:6]}),
    .in7({{29{1'b0}}, demultiplexer_3_out1_2[8:6]}), .out(multiplexer_5_out), .sel(instr));
  and and_1 (Carry, Enable, multiplexer_2_out);
  and and_2 (Imm32Enable, Enable, multiplexer_3_out);
  assign bit_extender_1_out = {{4{Enable}}, Enable};  // Bit_Extender bit_extender_1
  assign bit_extender_2_out = {{31{Enable}}, Enable};  // Bit_Extender bit_extender_2
  Multiplexer #(.select(3), .width(4), .enable("false")) multiplexer_6 (
    .in0(4'b0010), .in1(4'b0010), .in2(4'b0011), .in3(4'b0100), .in4(4'b0101), .in5(4'b0110), .in6(4'b0101),
    .in7(4'b0110), .out(multiplexer_6_out), .sel(instr));
  Multiplexer #(.select(3), .width(3), .enable("false")) multiplexer_7 (
    .in0(3'b000), .in1(demultiplexer_2_out0[5:3]), .in2(demultiplexer_2_out0[5:3]),
    .in3(demultiplexer_4_out0[2:0]), .in4(demultiplexer_3_out0[8:6]), .in5(demultiplexer_3_out0[8:6]),
    .in6(3'b000), .in7(3'b000), .out(multiplexer_7_out), .sel(instr));
  Multiplexer #(.select(3), .width(3), .enable("false")) multiplexer_8 (
    .in0(3'b000), .in1(3'b000), .in2(3'b000), .in3(3'b000), .in4(demultiplexer_3_out0_2),
    .in5(demultiplexer_3_out0_2), .in6(demultiplexer_3_out1_2[5:3]), .in7(demultiplexer_3_out1_2[5:3]),
    .out(multiplexer_8_out), .sel(instr));
  Multiplexer #(.select(3), .width(3), .enable("false")) multiplexer_9 (
    .in0(demultiplexer_1_out1[10:8]), .in1(demultiplexer_2_out0[2:0]), .in2(demultiplexer_2_out0[2:0]),
    .in3(demultiplexer_4_out0[5:3]), .in4(demultiplexer_3_out0[2:0]), .in5(demultiplexer_3_out0[2:0]),
    .in6(demultiplexer_3_out1), .in7(demultiplexer_3_out1), .out(multiplexer_9_out), .sel(instr));
  assign FUM = bit_extender_3_out & multiplexer_1_out;  // AND_Gate and_3, 4 bits wide
  assign Imm5 = bit_extender_1_out & multiplexer_4_out;  // AND_Gate and_4, 5 bits wide
  assign Imm32 = bit_extender_2_out & multiplexer_5_out;  // AND_Gate and_5, 32 bits wide
  assign bit_extender_3_out = {{3{Enable}}, Enable};  // Bit_Extender bit_extender_3
  assign bit_extender_4_out = {{2{Enable}}, Enable};  // Bit_Extender bit_extender_4
  assign codeAlu = bit_extender_3_out & multiplexer_6_out;  // AND_Gate and_6, 4 bits wide
  assign rm = bit_extender_4_out & multiplexer_7_out;  // AND_Gate and_7, 3 bits wide
  assign rn = bit_extender_4_out & multiplexer_8_out;  // AND_Gate and_8, 3 bits wide
  assign rd = bit_extender_4_out & multiplexer_9_out;  // AND_Gate and_9, 3 bits wide

  // Notes on the sheet:
  //   mov
  //   lsl & lsr
  //   asr
  //   register
  //   imm
  //   add & sub
endmodule

module Data_processing (
  input  [15:0] instruction,
  input  enable,
  output [2:0] Rm,
  output [2:0] Rn,
  output [2:0] Rd,
  output [3:0] ALU_opcode,
  output [3:0] FUM
);

  wire [3:0] bit_extender_2_out, FlagMaskCalculator_fum;
  wire [15:0] bit_extender_1_out;
  wire [15:10] and_1_out;

  assign bit_extender_1_out = {{15{enable}}, enable};  // Bit_Extender bit_extender_1
  assign {and_1_out, ALU_opcode, Rm, Rd} = instruction & bit_extender_1_out;  // AND_Gate and_1, 16 bits wide
  // Probe on {and_1_out, ALU_opcode, Rm, Rd}
  FlagMaskCalculator FlagMaskCalculator (.codeop(ALU_opcode), .FUM(FlagMaskCalculator_fum));
  assign bit_extender_2_out = {{3{enable}}, enable};  // Bit_Extender bit_extender_2
  assign FUM = FlagMaskCalculator_fum & bit_extender_2_out;  // AND_Gate and_2, 4 bits wide

  assign Rn = Rd;

  // Other names for the same wires on the sheet: r1[2:0] = Rd; r2[2:0] = Rm; alucode[3:0] = ALU_opcode;
  //   inst[15:0] = instruction
endmodule

module Load_Store (
  input  [15:0] instruction,
  input  enable,
  input  Clk,
  input  Reset,
  input  [31:0] Stack_pointer,
  output [2:0] Rm,
  output [2:0] Rd,
  output [31:0] RAM_Address,
  output PC_Hold,
  output Store,
  output Load
);

  wire and_2_out, not_1_out;
  wire [2:0] bit_extender_3_out, bit_extender_4_out, not_2_out;
  wire [31:0] adder_1_out, bit_extender_1_out, bit_extender_2_out;

  not not_1 (not_1_out, instruction[11]);
  and and_1 (Store, not_1_out, enable);
  and and_2 (and_2_out, instruction[11], enable);
  assign bit_extender_1_out = {{31{enable}}, enable};  // Bit_Extender bit_extender_1
  Adder #(.width(32)) adder_1 (.a(Stack_pointer), .b(bit_extender_2_out), .out(adder_1_out));  // open: cin, cout
  assign bit_extender_2_out = {{24{1'b0}}, instruction[7:0]};  // Bit_Extender bit_extender_2
  D_Flip_Flop d_ff_1 (.clk(Clk), .D(and_2_out), .Q(Load), .en(enable), .reset(Reset));  // open: Qn, preset
  assign RAM_Address = bit_extender_1_out & adder_1_out;  // AND_Gate and_3, 32 bits wide
  // Probe on RAM_Address
  assign bit_extender_3_out = {{2{instruction[11]}}, instruction[11]};  // Bit_Extender bit_extender_3
  assign not_2_out = ~bit_extender_3_out;  // NOT_Gate not_2, 3 bits wide
  assign bit_extender_4_out = {{2{enable}}, enable};  // Bit_Extender bit_extender_4
  assign Rd = not_2_out & bit_extender_4_out & instruction[10:8];  // AND_Gate and_4, 3 bits wide
  // Probe on Rd
  assign Rm = bit_extender_3_out & bit_extender_4_out & instruction[10:8];  // AND_Gate and_5, 3 bits wide
  // Probe on Rm

  assign PC_Hold = instruction[11];

  // Other names for the same wires on the sheet: imm8[7:0] = instruction[7:0]; rt[2:0] = instruction[10:8];
  //   _11 = instruction[11]; RAM_Ad[31:0] = RAM_Address; sp[31:0] = Stack_pointer

  // Notes on the sheet:
  //   0
  //   1
  //   0
endmodule

module SP_Address (
  input  enable,
  input  [15:0] instruction,
  input  [31:0] Stack_Pointer,
  output write_enable,
  output [31:0] New_Stack_Pointer
);

  wire [31:0] adder_1_out, bit_extender_1_out, multiplexer_1_out, subtractor_1_out;

  Adder #(.width(32)) adder_1 (
    .a({{25{1'b0}}, instruction[6:0]}), .b(Stack_Pointer), .out(adder_1_out));  // open: cin, cout
  Multiplexer #(.width(32), .enable("false")) multiplexer_1 (
    .in0(adder_1_out), .in1(subtractor_1_out), .out(multiplexer_1_out), .sel(instruction[7]));
  Subtractor #(.width(32)) subtractor_1 (
    .a({{25{1'b0}}, instruction[6:0]}), .b(Stack_Pointer), .out(subtractor_1_out));  // open: bin, bout
  assign bit_extender_1_out = {{31{enable}}, enable};  // Bit_Extender bit_extender_1
  assign New_Stack_Pointer = bit_extender_1_out & multiplexer_1_out;  // AND_Gate and_1, 32 bits wide

  assign write_enable = enable;
endmodule

module Conditionnal (
  input  Enable,
  input  [15:0] Instruction,
  input  N,
  input  Z,
  input  C,
  input  V,
  output [7:0] Offset,
  output Verified
);

  wire CC, comparator_3_eq, comparator_4_eq, comparator_5_eq, comparator_6_eq, comparator_10_gt,
       comparator_10_lt, comparator_11_eq, comparator_12_eq, comparator_13_eq, comparator_14_gt,
       comparator_14_lt, CS, EQ, GE, GT, HI, LE, LS, LT, MI, multiplexer_1_out, NE, or_2_out, PL, VC, VS;

  Comparator #(.width(1)) comparator_1 (.a(Z), .b(1'b1), .gt(NE), .eq(EQ));  // open: lt
  Comparator #(.width(1)) comparator_2 (.a(C), .b(1'b1), .gt(CC), .eq(CS));  // open: lt
  Comparator #(.width(1)) comparator_3 (.a(C), .b(1'b1), .eq(comparator_3_eq));  // open: gt, lt
  Comparator #(.width(1)) comparator_4 (.a(Z), .b(1'b0), .eq(comparator_4_eq));  // open: gt, lt
  Comparator #(.width(1)) comparator_5 (.a(C), .b(1'b0), .eq(comparator_5_eq));  // open: gt, lt
  Comparator #(.width(1)) comparator_6 (.a(Z), .b(1'b1), .eq(comparator_6_eq));  // open: gt, lt
  and and_1 (HI, comparator_3_eq, comparator_4_eq);
  and and_2 (LS, comparator_5_eq, comparator_6_eq);
  Comparator #(.width(1)) comparator_7 (.a(N), .b(1'b1), .gt(PL), .eq(MI));  // open: lt
  Comparator #(.width(1)) comparator_8 (.a(V), .b(1'b1), .gt(VC), .eq(VS));  // open: lt
  Comparator #(.width(1)) comparator_9 (.a(N), .b(V), .eq(GE));  // open: gt, lt
  or or_1 (LT, comparator_10_gt, comparator_10_lt);
  Comparator #(.width(1)) comparator_10 (.a(N), .b(V), .gt(comparator_10_gt), .lt(comparator_10_lt));  // open: eq
  Comparator #(.width(1)) comparator_11 (.a(Z), .b(1'b0), .eq(comparator_11_eq));  // open: gt, lt
  and and_3 (GT, comparator_11_eq, comparator_12_eq);
  Comparator #(.width(1)) comparator_12 (.a(N), .b(V), .eq(comparator_12_eq));  // open: gt, lt
  Comparator #(.width(1)) comparator_13 (.a(Z), .b(1'b1), .eq(comparator_13_eq));  // open: gt, lt
  or or_2 (or_2_out, comparator_14_gt, comparator_14_lt);
  Comparator #(.width(1)) comparator_14 (.a(Z), .b(V), .gt(comparator_14_gt), .lt(comparator_14_lt));  // open: eq
  Multiplexer #(.select(4)) multiplexer_1 (
    .in0(EQ), .in1(NE), .in2(CS), .in3(CC), .in4(MI), .in5(PL), .in6(VS), .in7(VC), .in8(HI), .in9(LS),
    .in10(GE), .in11(LT), .in12(GT), .in13(LE), .in14(1'b1), .out(multiplexer_1_out), .sel(Instruction[11:8]));  // open: in15, en
  or or_3 (LE, comparator_13_eq, or_2_out);
  assign Offset = Verified ? Instruction[7:0] : 8'bz;  // Controlled_Buffer controlled_buffer_1
  and and_4 (Verified, multiplexer_1_out, Enable);

  // Other names for the same wires on the sheet: imm8[7:0] = Instruction[7:0]; select[3:0] = Instruction[11:8]
endmodule

module FlagAPSR (
  input  [3:0] flagsin,
  input  [3:0] FUM,
  input  clk,
  input  reset,
  output [3:0] flagsout
);

  wire comparator_1_lt, comparator_2_lt, comparator_3_lt, comparator_4_lt;

  Comparator #(.width(1)) comparator_1 (.a(FUM[3]), .b(1'b0), .lt(comparator_1_lt));  // open: gt, eq
  Comparator #(.width(1)) comparator_2 (.a(FUM[2]), .b(1'b0), .lt(comparator_2_lt));  // open: gt, eq
  Comparator #(.width(1)) comparator_3 (.a(FUM[1]), .b(1'b0), .lt(comparator_3_lt));  // open: gt, eq
  Comparator #(.width(1)) comparator_4 (.a(FUM[0]), .b(1'b0), .lt(comparator_4_lt));  // open: gt, eq
  and and_1 (flagsout[3], flagsin[3], comparator_1_lt);
  and and_2 (flagsout[2], flagsin[2], comparator_2_lt);
  and and_3 (flagsout[1], flagsin[1], comparator_3_lt);
  and and_4 (flagsout[0], flagsin[0], comparator_4_lt);

  // Other names for the same wires on the sheet: newV = flagsin[0]; newC = flagsin[1]; newZ = flagsin[2];
  //   newN = flagsin[3]; FlagsV = flagsout[0]; FlagsC = flagsout[1]; FlagsZ = flagsout[2]; FlagsN = flagsout[3];
  //   updateMask[3:0] = FUM; V = FUM[0]; C = FUM[1]; Z = FUM[2]; N = FUM[3]
endmodule

module FlagMaskCalculator (
  input  [3:0] codeop,
  output [3:0] FUM
);

  wire and_1_out, and_2_out, and_3_out, and_4_out, and_5_out, not_1_out, not_2_out, not_3_out, not_4_out,
       not_5_out, not_6_out, not_7_out;

  not not_1 (not_1_out, codeop[2]);
  not not_2 (not_2_out, codeop[3]);
  not not_3 (not_3_out, codeop[3]);
  not not_4 (not_4_out, codeop[1]);
  not not_5 (not_5_out, codeop[3]);
  not not_6 (not_6_out, codeop[0]);
  not not_7 (not_7_out, codeop[2]);
  and and_1 (and_1_out, not_1_out, codeop[1]);
  and and_2 (and_2_out, not_2_out, codeop[2]);
  and and_3 (and_3_out, not_3_out, codeop[2], not_4_out, codeop[0]);
  and and_4 (and_4_out, not_5_out, codeop[2], codeop[1], not_6_out);
  and and_5 (and_5_out, codeop[3], not_7_out, codeop[1]);
  or or_1 (FUM[1], and_1_out, and_2_out);
  or or_2 (FUM[0], and_3_out, and_4_out, and_5_out);

  assign FUM[3:2] = 2'b11;
endmodule

module opcode_decoder (
  input  _1,
  input  _2,
  input  _3,
  input  _4,
  input  _5,
  input  _6,
  input  _7,
  output [2:0] instr
);

  wire and_2_out, and_3_out, and_4_out, and_5_out, and_6_out, and_7_out, and_8_out, not_1_out, not_2_out,
       not_3_out, not_4_out, not_5_out, not_6_out, not_7_out, not_8_out, not_9_out, not_10_out, not_11_out,
       not_12_out, not_13_out, not_14_out;

  not not_1 (not_1_out, _1);
  not not_2 (not_2_out, _1);
  not not_3 (not_3_out, _2);
  not not_4 (not_4_out, _1);
  not not_5 (not_5_out, _4);
  not not_6 (not_6_out, _1);
  not not_7 (not_7_out, _1);
  not not_8 (not_8_out, _2);
  not not_9 (not_9_out, _3);
  not not_10 (not_10_out, _1);
  not not_11 (not_11_out, _4);
  not not_12 (not_12_out, _1);
  not not_13 (not_13_out, _5);
  not not_14 (not_14_out, _1);
  and and_1 (instr[2], not_1_out, _2, _4);
  and and_2 (and_2_out, not_2_out, not_3_out, _3);
  and and_3 (and_3_out, not_4_out, _2, not_5_out);
  and and_4 (and_4_out, not_6_out, _2, _5);
  and and_5 (and_5_out, not_7_out, not_8_out, not_9_out);
  and and_6 (and_6_out, not_10_out, _2, not_11_out);
  and and_7 (and_7_out, not_12_out, _2, not_13_out, _6);
  and and_8 (and_8_out, not_14_out, _2, _5, _7);
  or or_1 (instr[1], and_2_out, and_3_out, and_4_out);
  or or_2 (instr[0], and_5_out, and_6_out, and_7_out, and_8_out);
endmodule

module decoder (
  input  [5:0] Opcode,
  output a,
  output b,
  output c,
  output d,
  output e
);

  wire and_2_out, and_3_out, and_4_out, and_5_out, and_6_out, and_7_out, and_8_out, and_9_out, and_10_out,
       and_11_out, not_1_out, not_2_out, not_3_out, not_4_out, not_5_out, not_6_out, not_7_out, not_8_out,
       not_9_out, not_10_out, not_11_out;

  not not_1 (not_1_out, Opcode[5]);
  and and_1 (a, not_1_out, not_2_out);
  not not_2 (not_2_out, Opcode[4]);
  not not_3 (not_3_out, Opcode[5]);
  and and_2 (and_2_out, not_3_out, Opcode[4]);
  not not_4 (not_4_out, Opcode[3]);
  not not_5 (not_5_out, Opcode[2]);
  and and_3 (and_3_out, not_5_out, not_6_out);
  not not_6 (not_6_out, Opcode[1]);
  not not_7 (not_7_out, Opcode[0]);
  and and_4 (and_4_out, Opcode[5], not_8_out);
  not not_8 (not_8_out, Opcode[4]);
  not not_9 (not_9_out, Opcode[3]);
  and and_5 (and_5_out, not_9_out, Opcode[2]);
  and and_6 (and_6_out, Opcode[5], not_10_out);
  not not_10 (not_10_out, Opcode[4]);
  and and_7 (and_7_out, Opcode[3], Opcode[2]);
  and and_8 (and_8_out, Opcode[5], Opcode[4]);
  not not_11 (not_11_out, Opcode[3]);
  and and_9 (and_9_out, not_11_out, Opcode[2]);
  and and_10 (and_10_out, and_2_out, not_4_out);
  and and_11 (and_11_out, and_3_out, not_7_out);
  and and_12 (c, and_4_out, and_5_out);
  and and_13 (d, and_6_out, and_7_out);
  and and_14 (e, and_8_out, and_9_out);
  and and_15 (b, and_10_out, and_11_out);
endmodule
