// Logisim project ual.circ as structural Verilog: 1 circuit, main circuit main
module main (
  input  [31:0] A,
  input  [31:0] B,
  input  [4:0] shift,
  input  c_in,
  input  [3:0] codop,
  output [31:0] S,
  output [3:0] flags
);

  wire bitselector_2_out, bitselector_3_out, bitselector_4_out, bitselector_5_out, bitselector_6_out,
       bitselector_7_out, c_out_2, c_out_3_4, c_out_5, c_out_6, c_out_7, c_out_10, c_out_11, n_8, n_10, n_11,
       n_all, not_1_out, v_5_11, v_6_10, xnor_1_out, xnor_2_out, xor_2_out, xor_3_out, z_8, z_10, z_11, z_all;
  wire [4:0] subtractor_4_out, subtractor_5_out;
  wire [31:0] ADC, AND, ASR, BIC, CMN, CMP, EOR, LSL, LSR, MUL, MVN, ORR, ROR, RSB, SBC;

  not not_1 (not_1_out, c_in);
  assign ORR = A | B;  // OR_Gate or_1, 32 bits wide
  assign BIC = A & MVN;  // AND_Gate and_1, 32 bits wide
  assign MVN = ~B;  // NOT_Gate not_2, 32 bits wide
  assign AND = A & B;  // AND_Gate and_2, 32 bits wide
  assign EOR = A ^ B;  // XOR_Gate xor_1, 32 bits wide
  Shifter #(.width(32)) shifter_1 (.in(B), .\dist (shift), .out(LSL));
  Shifter #(.width(32), .shift("lr")) shifter_2 (.in(B), .\dist (shift), .out(LSR));
  Shifter #(.width(32), .shift("ar")) shifter_3 (.in(B), .\dist (shift), .out(ASR));
  Adder #(.width(32)) adder_1 (.a(A), .b(B), .out(ADC), .cin(c_in), .cout(c_out_5));
  Subtractor #(.width(32)) subtractor_1 (.a(A), .b(B), .out(SBC), .bin(not_1_out), .bout(c_out_6));
  Shifter #(.width(32), .shift("rr")) shifter_4 (.in(B), .\dist (shift), .out(ROR));
  Comparator #(.width(32)) comparator_1 (.a(AND), .b({32{1'b0}}), .eq(z_8), .lt(n_8));  // open: gt
  Subtractor #(.width(32)) subtractor_2 (.a({32{1'b0}}), .b(A), .out(RSB));  // open: bin, bout
  Subtractor #(.width(32)) subtractor_3 (.a(A), .b(B), .out(CMP), .bout(c_out_10));  // open: bin
  Comparator #(.width(32)) comparator_2 (.a(CMP), .b({32{1'b0}}), .eq(z_10), .lt(n_10));  // open: gt
  Adder #(.width(32)) adder_2 (.a(A), .b(B), .out(CMN), .cout(c_out_11));  // open: cin
  Comparator #(.width(32)) comparator_3 (.a(CMN), .b({32{1'b0}}), .eq(z_11), .lt(n_11));  // open: gt
  Multiplier #(.width(32)) multiplier_1 (.a(A), .b(B), .out(MUL));  // open: cin, cout
  Subtractor #(.width(5)) subtractor_4 (.a({5{1'b1}}), .b(shift), .out(subtractor_4_out));  // open: bin, bout
  Subtractor #(.width(5)) subtractor_5 (.a(shift), .b(5'b00001), .out(subtractor_5_out));  // open: bin, bout
  BitSelector #(.width(32)) bitselector_1 (.in(ROR), .out(c_out_7), .sel({5{1'b1}}));
  BitSelector #(.width(32)) bitselector_2 (.in(A), .out(bitselector_2_out), .sel({5{1'b1}}));
  BitSelector #(.width(32)) bitselector_3 (.in(B), .out(bitselector_3_out), .sel({5{1'b1}}));
  BitSelector #(.width(32)) bitselector_4 (.in(S), .out(bitselector_4_out), .sel({5{1'b1}}));
  BitSelector #(.width(32)) bitselector_5 (.in(A), .out(bitselector_5_out), .sel({5{1'b1}}));
  BitSelector #(.width(32)) bitselector_6 (.in(B), .out(bitselector_6_out), .sel({5{1'b1}}));
  BitSelector #(.width(32)) bitselector_7 (.in(S), .out(bitselector_7_out), .sel({5{1'b1}}));
  BitSelector #(.width(32)) bitselector_8 (.in(B), .out(c_out_2), .sel(subtractor_4_out));
  BitSelector #(.width(32)) bitselector_9 (.in(B), .out(c_out_3_4), .sel(subtractor_5_out));
  xor xor_2 (xor_2_out, bitselector_2_out, bitselector_3_out);
  xnor xnor_1 (xnor_1_out, bitselector_3_out, bitselector_4_out);
  xnor xnor_2 (xnor_2_out, bitselector_5_out, bitselector_6_out);
  xor xor_3 (xor_3_out, bitselector_6_out, bitselector_7_out);
  and and_3 (v_6_10, xor_2_out, xnor_1_out);
  and and_4 (v_5_11, xnor_2_out, xor_3_out);
  Comparator #(.width(32)) comparator_4 (.a(S), .b({32{1'b0}}), .eq(z_all), .lt(n_all));  // open: gt
  Multiplexer #(.select(4)) multiplexer_1 (
    .in0(n_all), .in1(n_all), .in2(n_all), .in3(n_all), .in4(n_all), .in5(n_all), .in6(n_all), .in7(n_all),
    .in8(n_8), .in9(n_all), .in10(n_10), .in11(n_11), .in12(n_all), .in13(n_all), .in14(n_all), .in15(n_all),
    .out(flags[3]), .sel(codop), .en(1'b1));
  Multiplexer #(.select(4)) multiplexer_2 (
    .in0(1'b0), .in1(1'b0), .in2(c_out_2), .in3(c_out_3_4), .in4(c_out_3_4), .in5(c_out_5), .in6(c_out_6),
    .in7(c_out_7), .in8(1'b0), .in9(1'b0), .in10(1'b0), .in11(1'b0), .in12(1'b0), .in13(1'b0), .in14(1'b0),
    .in15(1'b0), .out(flags[1]), .sel(codop), .en(1'b1));
  Multiplexer #(.select(4), .width(32)) multiplexer_3 (
    .in0(AND), .in1(EOR), .in2(LSL), .in3(LSR), .in4(ASR), .in5(ADC), .in6(SBC), .in7(ROR), .in9(RSB),
    .in12(ORR), .in13(MUL), .in14(BIC), .in15(MVN), .out(S), .sel(codop), .en(1'b1));  // open: in8, in10, in11
  Multiplexer #(.select(4)) multiplexer_4 (
    .in0(z_all), .in1(z_all), .in2(z_all), .in3(z_all), .in4(z_all), .in5(z_all), .in6(z_all), .in7(z_all),
    .in8(z_8), .in9(z_all), .in10(z_10), .in11(z_11), .in12(z_all), .in13(z_all), .in14(z_all), .in15(z_all),
    .out(flags[2]), .sel(codop), .en(1'b1));
  Multiplexer #(.select(4)) multiplexer_5 (
    .in0(1'b0), .in1(1'b0), .in2(1'b0), .in3(1'b0), .in4(1'b0), .in5(v_5_11), .in6(v_6_10), .in7(1'b0),
    .in8(1'b0), .in9(1'b0), .in10(v_6_10), .in11(v_5_11), .in12(1'b0), .in13(1'b0), .in14(1'b0), .in15(1'b0),
    .out(flags[0]), .sel(codop), .en(1'b1));

  // Other names for the same wires on the sheet: v = flags[0]; c = flags[1]; z = flags[2]; n = flags[3]

  // Notes on the sheet:
  //   Entrées
  //   Sorties
  //   NZCV
  //   Opérations
  //   0) AND (A and B)
  //   1) EOR (A xor B)
  //   2) LSL (B << shift)
  //   3) LSR (B >> shift)
  //   4) ASR (B >> shift (arith))
  //   5) ADC (A + B + c-in)
  //   6) SBC (A - B + c-in - 1)
  //   7) ROR (B >> shift (rot))
  //   12) ORR (A or B)
  //   13) MUL (A * B)
  //   14) BIC (A and not B)
  //   15) MVN (not B)
  //   8) TST (A and B, résultat perdu, drapeaux mis à jour)
  //   9) RSB (0 - A, registre Rm utilisé plutôt que Rn)
  //   10) CMP (A - B, résultat perdu, drapeaux mis à jour)
  //   11) CMN (A + B, résultat perdu, drapeaux mis à jour)
  //   Rq : on compare les signes (le dernier bit) de a, b et s pour détecter des cas où on peut avoir un overflow
  //   Mise à jour des drapeaux
  //   Negative
  //   CarryOut
  //   Rq : les drapeaux N et Z sont les mêmes pour toutes les opérations qui renvoient un résultat
  //   pour les opérations qui ne renvoient pas de résultat, on doit les récupérer séparement
  //   Zero
  //   oVerflow
  //   Récupération des résultats
endmodule
